// Logisim project CPU.circ as structural Verilog: 7 circuits, main circuit main
// A
module main (
  input  sa,
  input  in_2,
  input  [7:0] in_3
);

  wire decoder_1_out0, decoder_1_out1, decoder_1_out2, decoder_1_out3, decoder_1_out4, decoder_2_out0,
       decoder_2_out1, undriven, undriven_2, undriven_3, undriven_4, undriven_5, undriven_6;
  wire [7:0] n8register_1_out_4;

  _8Register u_8register_1 (.out_4(n8register_1_out_4), .in_2(in_3), .in_3(in_2), .in_1(sa));
  Decoder #(.enable("false"), .select(4)) decoder_1 (
    .out0(decoder_1_out0), .out1(decoder_1_out1), .out2(decoder_1_out2), .out3(decoder_1_out3),
    .out4(decoder_1_out4), .sel(n8register_1_out_4[7:4]));  // open: out5, out6, out7, out8, out9, out10, out11, out12, out13, out14, out15
  DRAM_1BYTE dram_1byte_1 (.Y(decoder_1_out0), .X(decoder_2_out0));  // open: b_o, b_s, b_e, b_i
  DRAM_1BYTE dram_1byte_2 (.Y(decoder_1_out1), .X(decoder_2_out0));  // open: b_o, b_s, b_e, b_i
  DRAM_1BYTE dram_1byte_3 (.Y(decoder_1_out2), .X(decoder_2_out0));  // open: b_o, b_s, b_e, b_i
  DRAM_1BYTE dram_1byte_4 (.Y(decoder_1_out3), .X(decoder_2_out0));  // open: b_o, b_s, b_e, b_i
  DRAM_1BYTE dram_1byte_5 (.Y(decoder_1_out4), .X(decoder_2_out0));  // open: b_o, b_s, b_e, b_i
  DRAM_1BYTE dram_1byte_6 (.Y(undriven));  // open: b_o, X, b_s, b_e, b_i
  DRAM_1BYTE dram_1byte_7 (.Y(undriven_2));  // open: b_o, X, b_s, b_e, b_i
  DRAM_1BYTE dram_1byte_8 (.Y(undriven_3));  // open: b_o, X, b_s, b_e, b_i
  DRAM_1BYTE dram_1byte_9 ();  // open: b_o, Y, X, b_s, b_e, b_i
  DRAM_1BYTE dram_1byte_10 ();  // open: b_o, Y, X, b_s, b_e, b_i
  DRAM_1BYTE dram_1byte_11 ();  // open: b_o, Y, X, b_s, b_e, b_i
  DRAM_1BYTE dram_1byte_12 ();  // open: b_o, Y, X, b_s, b_e, b_i
  DRAM_1BYTE dram_1byte_13 ();  // open: b_o, Y, X, b_s, b_e, b_i
  DRAM_1BYTE dram_1byte_14 ();  // open: b_o, Y, X, b_s, b_e, b_i
  DRAM_1BYTE dram_1byte_15 ();  // open: b_o, Y, X, b_s, b_e, b_i
  DRAM_1BYTE dram_1byte_16 ();  // open: b_o, Y, X, b_s, b_e, b_i
  DRAM_1BYTE dram_1byte_17 (.Y(decoder_1_out0), .X(decoder_2_out1));  // open: b_o, b_s, b_e, b_i
  DRAM_1BYTE dram_1byte_18 (.Y(decoder_1_out1), .X(decoder_2_out1));  // open: b_o, b_s, b_e, b_i
  DRAM_1BYTE dram_1byte_19 (.Y(decoder_1_out2), .X(decoder_2_out1));  // open: b_o, b_s, b_e, b_i
  DRAM_1BYTE dram_1byte_20 (.Y(decoder_1_out3), .X(decoder_2_out1));  // open: b_o, b_s, b_e, b_i
  DRAM_1BYTE dram_1byte_21 (.Y(decoder_1_out4), .X(decoder_2_out1));  // open: b_o, b_s, b_e, b_i
  DRAM_1BYTE dram_1byte_22 (.Y(undriven_4));  // open: b_o, X, b_s, b_e, b_i
  DRAM_1BYTE dram_1byte_23 (.Y(undriven_5));  // open: b_o, X, b_s, b_e, b_i
  DRAM_1BYTE dram_1byte_24 (.Y(undriven_6));  // open: b_o, X, b_s, b_e, b_i
  DRAM_1BYTE dram_1byte_25 ();  // open: b_o, Y, X, b_s, b_e, b_i
  DRAM_1BYTE dram_1byte_26 ();  // open: b_o, Y, X, b_s, b_e, b_i
  DRAM_1BYTE dram_1byte_27 ();  // open: b_o, Y, X, b_s, b_e, b_i
  DRAM_1BYTE dram_1byte_28 ();  // open: b_o, Y, X, b_s, b_e, b_i
  DRAM_1BYTE dram_1byte_29 ();  // open: b_o, Y, X, b_s, b_e, b_i
  DRAM_1BYTE dram_1byte_30 ();  // open: b_o, Y, X, b_s, b_e, b_i
  DRAM_1BYTE dram_1byte_31 ();  // open: b_o, Y, X, b_s, b_e, b_i
  DRAM_1BYTE dram_1byte_32 ();  // open: b_o, Y, X, b_s, b_e, b_i
  Decoder #(.enable("false"), .select(4)) decoder_2 (
    .out0(decoder_2_out0), .out1(decoder_2_out1));  // open: out2, out3, out4, out5, out6, out7, out8, out9, out10, out11, out12, out13, out14, out15, sel
  DRAM_1BYTE dram_1byte_33 ();  // open: b_o, Y, X, b_s, b_e, b_i
  DRAM_1BYTE dram_1byte_34 ();  // open: b_o, Y, X, b_s, b_e, b_i
  DRAM_1BYTE dram_1byte_35 ();  // open: b_o, Y, X, b_s, b_e, b_i
  DRAM_1BYTE dram_1byte_36 ();  // open: b_o, Y, X, b_s, b_e, b_i
  DRAM_1BYTE dram_1byte_37 ();  // open: b_o, Y, X, b_s, b_e, b_i
  DRAM_1BYTE dram_1byte_38 ();  // open: b_o, Y, X, b_s, b_e, b_i
  DRAM_1BYTE dram_1byte_39 ();  // open: b_o, Y, X, b_s, b_e, b_i
  DRAM_1BYTE dram_1byte_40 ();  // open: b_o, Y, X, b_s, b_e, b_i
  DRAM_1BYTE dram_1byte_41 ();  // open: b_o, Y, X, b_s, b_e, b_i
  DRAM_1BYTE dram_1byte_42 ();  // open: b_o, Y, X, b_s, b_e, b_i
  DRAM_1BYTE dram_1byte_43 ();  // open: b_o, Y, X, b_s, b_e, b_i
  DRAM_1BYTE dram_1byte_44 ();  // open: b_o, Y, X, b_s, b_e, b_i
  DRAM_1BYTE dram_1byte_45 ();  // open: b_o, Y, X, b_s, b_e, b_i
  DRAM_1BYTE dram_1byte_46 ();  // open: b_o, Y, X, b_s, b_e, b_i
  DRAM_1BYTE dram_1byte_47 ();  // open: b_o, Y, X, b_s, b_e, b_i
  DRAM_1BYTE dram_1byte_48 ();  // open: b_o, Y, X, b_s, b_e, b_i
  DRAM_1BYTE dram_1byte_49 ();  // open: b_o, Y, X, b_s, b_e, b_i
  DRAM_1BYTE dram_1byte_50 ();  // open: b_o, Y, X, b_s, b_e, b_i
  DRAM_1BYTE dram_1byte_51 ();  // open: b_o, Y, X, b_s, b_e, b_i
  DRAM_1BYTE dram_1byte_52 ();  // open: b_o, Y, X, b_s, b_e, b_i
  DRAM_1BYTE dram_1byte_53 ();  // open: b_o, Y, X, b_s, b_e, b_i
  DRAM_1BYTE dram_1byte_54 ();  // open: b_o, Y, X, b_s, b_e, b_i
  DRAM_1BYTE dram_1byte_55 ();  // open: b_o, Y, X, b_s, b_e, b_i
  DRAM_1BYTE dram_1byte_56 ();  // open: b_o, Y, X, b_s, b_e, b_i
  DRAM_1BYTE dram_1byte_57 ();  // open: b_o, Y, X, b_s, b_e, b_i
  DRAM_1BYTE dram_1byte_58 ();  // open: b_o, Y, X, b_s, b_e, b_i
  DRAM_1BYTE dram_1byte_59 ();  // open: b_o, Y, X, b_s, b_e, b_i
  DRAM_1BYTE dram_1byte_60 ();  // open: b_o, Y, X, b_s, b_e, b_i
  DRAM_1BYTE dram_1byte_61 ();  // open: b_o, Y, X, b_s, b_e, b_i
  DRAM_1BYTE dram_1byte_62 ();  // open: b_o, Y, X, b_s, b_e, b_i
  DRAM_1BYTE dram_1byte_63 ();  // open: b_o, Y, X, b_s, b_e, b_i
  DRAM_1BYTE dram_1byte_64 ();  // open: b_o, Y, X, b_s, b_e, b_i
  DRAM_1BYTE dram_1byte_65 ();  // open: b_o, Y, X, b_s, b_e, b_i
  DRAM_1BYTE dram_1byte_66 ();  // open: b_o, Y, X, b_s, b_e, b_i
  DRAM_1BYTE dram_1byte_67 ();  // open: b_o, Y, X, b_s, b_e, b_i
  DRAM_1BYTE dram_1byte_68 ();  // open: b_o, Y, X, b_s, b_e, b_i
  DRAM_1BYTE dram_1byte_69 ();  // open: b_o, Y, X, b_s, b_e, b_i
  DRAM_1BYTE dram_1byte_70 ();  // open: b_o, Y, X, b_s, b_e, b_i
  DRAM_1BYTE dram_1byte_71 ();  // open: b_o, Y, X, b_s, b_e, b_i
  DRAM_1BYTE dram_1byte_72 ();  // open: b_o, Y, X, b_s, b_e, b_i
  DRAM_1BYTE dram_1byte_73 ();  // open: b_o, Y, X, b_s, b_e, b_i
  DRAM_1BYTE dram_1byte_74 ();  // open: b_o, Y, X, b_s, b_e, b_i
  DRAM_1BYTE dram_1byte_75 ();  // open: b_o, Y, X, b_s, b_e, b_i
  DRAM_1BYTE dram_1byte_76 ();  // open: b_o, Y, X, b_s, b_e, b_i
  DRAM_1BYTE dram_1byte_77 ();  // open: b_o, Y, X, b_s, b_e, b_i
  DRAM_1BYTE dram_1byte_78 ();  // open: b_o, Y, X, b_s, b_e, b_i
  DRAM_1BYTE dram_1byte_79 ();  // open: b_o, Y, X, b_s, b_e, b_i
  DRAM_1BYTE dram_1byte_80 ();  // open: b_o, Y, X, b_s, b_e, b_i
  DRAM_1BYTE dram_1byte_81 ();  // open: b_o, Y, X, b_s, b_e, b_i
  DRAM_1BYTE dram_1byte_82 ();  // open: b_o, Y, X, b_s, b_e, b_i
  DRAM_1BYTE dram_1byte_83 ();  // open: b_o, Y, X, b_s, b_e, b_i
  DRAM_1BYTE dram_1byte_84 ();  // open: b_o, Y, X, b_s, b_e, b_i
  DRAM_1BYTE dram_1byte_85 ();  // open: b_o, Y, X, b_s, b_e, b_i
  DRAM_1BYTE dram_1byte_86 ();  // open: b_o, Y, X, b_s, b_e, b_i
  DRAM_1BYTE dram_1byte_87 ();  // open: b_o, Y, X, b_s, b_e, b_i
  DRAM_1BYTE dram_1byte_88 ();  // open: b_o, Y, X, b_s, b_e, b_i
  DRAM_1BYTE dram_1byte_89 ();  // open: b_o, Y, X, b_s, b_e, b_i
  DRAM_1BYTE dram_1byte_90 ();  // open: b_o, Y, X, b_s, b_e, b_i
  DRAM_1BYTE dram_1byte_91 ();  // open: b_o, Y, X, b_s, b_e, b_i
  DRAM_1BYTE dram_1byte_92 ();  // open: b_o, Y, X, b_s, b_e, b_i
  DRAM_1BYTE dram_1byte_93 ();  // open: b_o, Y, X, b_s, b_e, b_i
  DRAM_1BYTE dram_1byte_94 ();  // open: b_o, Y, X, b_s, b_e, b_i
  DRAM_1BYTE dram_1byte_95 ();  // open: b_o, Y, X, b_s, b_e, b_i
  DRAM_1BYTE dram_1byte_96 ();  // open: b_o, Y, X, b_s, b_e, b_i
  DRAM_1BYTE dram_1byte_97 ();  // open: b_o, Y, X, b_s, b_e, b_i
  DRAM_1BYTE dram_1byte_98 ();  // open: b_o, Y, X, b_s, b_e, b_i
  DRAM_1BYTE dram_1byte_99 ();  // open: b_o, Y, X, b_s, b_e, b_i
  DRAM_1BYTE dram_1byte_100 ();  // open: b_o, Y, X, b_s, b_e, b_i
  DRAM_1BYTE dram_1byte_101 ();  // open: b_o, Y, X, b_s, b_e, b_i
  DRAM_1BYTE dram_1byte_102 ();  // open: b_o, Y, X, b_s, b_e, b_i
  DRAM_1BYTE dram_1byte_103 ();  // open: b_o, Y, X, b_s, b_e, b_i
  DRAM_1BYTE dram_1byte_104 ();  // open: b_o, Y, X, b_s, b_e, b_i
  DRAM_1BYTE dram_1byte_105 ();  // open: b_o, Y, X, b_s, b_e, b_i
  DRAM_1BYTE dram_1byte_106 ();  // open: b_o, Y, X, b_s, b_e, b_i
  DRAM_1BYTE dram_1byte_107 ();  // open: b_o, Y, X, b_s, b_e, b_i
  DRAM_1BYTE dram_1byte_108 ();  // open: b_o, Y, X, b_s, b_e, b_i
  DRAM_1BYTE dram_1byte_109 ();  // open: b_o, Y, X, b_s, b_e, b_i
  DRAM_1BYTE dram_1byte_110 ();  // open: b_o, Y, X, b_s, b_e, b_i
  DRAM_1BYTE dram_1byte_111 ();  // open: b_o, Y, X, b_s, b_e, b_i
  DRAM_1BYTE dram_1byte_112 ();  // open: b_o, Y, X, b_s, b_e, b_i
  DRAM_1BYTE dram_1byte_113 ();  // open: b_o, Y, X, b_s, b_e, b_i
  DRAM_1BYTE dram_1byte_114 ();  // open: b_o, Y, X, b_s, b_e, b_i
  DRAM_1BYTE dram_1byte_115 ();  // open: b_o, Y, X, b_s, b_e, b_i
  DRAM_1BYTE dram_1byte_116 ();  // open: b_o, Y, X, b_s, b_e, b_i
  DRAM_1BYTE dram_1byte_117 ();  // open: b_o, Y, X, b_s, b_e, b_i
  DRAM_1BYTE dram_1byte_118 ();  // open: b_o, Y, X, b_s, b_e, b_i
  DRAM_1BYTE dram_1byte_119 ();  // open: b_o, Y, X, b_s, b_e, b_i
  DRAM_1BYTE dram_1byte_120 ();  // open: b_o, Y, X, b_s, b_e, b_i
  DRAM_1BYTE dram_1byte_121 ();  // open: b_o, Y, X, b_s, b_e, b_i
  DRAM_1BYTE dram_1byte_122 ();  // open: b_o, Y, X, b_s, b_e, b_i
  DRAM_1BYTE dram_1byte_123 ();  // open: b_o, Y, X, b_s, b_e, b_i
  DRAM_1BYTE dram_1byte_124 ();  // open: b_o, Y, X, b_s, b_e, b_i
  DRAM_1BYTE dram_1byte_125 ();  // open: b_o, Y, X, b_s, b_e, b_i
  DRAM_1BYTE dram_1byte_126 ();  // open: b_o, Y, X, b_s, b_e, b_i
  DRAM_1BYTE dram_1byte_127 ();  // open: b_o, Y, X, b_s, b_e, b_i
  DRAM_1BYTE dram_1byte_128 ();  // open: b_o, Y, X, b_s, b_e, b_i
endmodule

module _1M (
  input  I,
  input  S,
  output O
);

  wire _1_out, _2_out, _4_out;

  nand _1 (_1_out, I, S);
  nand _2 (_2_out, _1_out, S);
  nand _3 (O, _1_out, _4_out);
  nand _4 (_4_out, O, _2_out);
endmodule

module _8M (
  input  in_1,
  input  [7:0] in_2,
  output [7:0] out_3
);

  _1M u_1m_1 (.O(out_3[0]), .S(in_1), .I(in_2[0]));
  _1M u_1m_2 (.O(out_3[1]), .S(in_1), .I(in_2[1]));
  _1M u_1m_3 (.O(out_3[2]), .S(in_1), .I(in_2[2]));
  _1M u_1m_4 (.O(out_3[3]), .S(in_1), .I(in_2[3]));
  _1M u_1m_5 (.O(out_3[4]), .S(in_1), .I(in_2[4]));
  _1M u_1m_6 (.O(out_3[5]), .S(in_1), .I(in_2[5]));
  _1M u_1m_7 (.O(out_3[6]), .S(in_1), .I(in_2[6]));
  _1M u_1m_8 (.O(out_3[7]), .S(in_1), .I(in_2[7]));
endmodule

module _8Register (
  input  in_1,
  input  [7:0] in_2,
  input  in_3,
  output [7:0] out_4
);

  wire [7:0] controlled_buffer_1_out, enabler_1_out_3, n8m_1_out_3;

  assign controlled_buffer_1_out = in_1 ? in_2 : 8'bz;  // Controlled_Buffer controlled_buffer_1
  _8M u_8m_1 (.in_1(in_1), .in_2(controlled_buffer_1_out), .out_3(n8m_1_out_3));
  assign out_4 = in_3 ? enabler_1_out_3 : 8'bz;  // Controlled_Buffer controlled_buffer_2
  enabler enabler_1 (.in_1(n8m_1_out_3), .in_2(in_3), .out_3(enabler_1_out_3));
endmodule

module enabler (
  input  [7:0] in_1,
  input  in_2,
  output [7:0] out_3
);

  and and_1 (out_3[0], in_2, in_1[0]);
  and and_2 (out_3[1], in_2, in_1[1]);
  and and_3 (out_3[2], in_2, in_1[2]);
  and and_4 (out_3[3], in_2, in_1[3]);
  and and_5 (out_3[4], in_2, in_1[4]);
  and and_6 (out_3[5], in_2, in_1[5]);
  and and_7 (out_3[6], in_2, in_1[6]);
  and and_8 (out_3[7], in_2, in_1[7]);
endmodule

module Bus_Copy (
  input  in_1,
  input  in_2,
  input  in_3,
  input  in_4,
  input  [7:0] in_5,
  output [7:0] out_6,
  output [7:0] out_7,
  output [7:0] out_8
);

  wire and_1_out, not_1_out, not_2_out;

  not not_1 (not_1_out, in_4);
  not not_2 (not_2_out, in_3);
  and and_1 (and_1_out, not_1_out, not_2_out);
  assign out_8 = and_1_out ? in_5 : 8'bz;  // Controlled_Buffer in_Buff
  _8Register RA (.out_4(out_6), .in_2(out_8), .in_3(in_3), .in_1(in_1));
  assign out_8 = in_3 ? out_6 : 8'bz;  // Controlled_Buffer out_BuffA
  _8Register RB (.out_4(out_7), .in_2(out_8), .in_3(in_4), .in_1(in_2));
  assign out_8 = in_4 ? out_7 : 8'bz;  // Controlled_Buffer out_BuffB
endmodule

module DRAM_1BYTE (
  input  Y,
  input  X,
  input  b_s,
  input  b_e,
  input  [7:0] b_i,
  output [7:0] b_o
);

  wire and_e_out, and_s_out, end_ad_out;
  wire [7:0] controlled_buffer_1_out, n8register_1_out_4;

  and end_ad (end_ad_out, Y, X);
  assign controlled_buffer_1_out = end_ad_out ? b_i : 8'bz;  // Controlled_Buffer controlled_buffer_1
  assign b_o = end_ad_out ? n8register_1_out_4 : 8'bz;  // Controlled_Buffer controlled_buffer_2
  and and_s (and_s_out, end_ad_out, b_s);
  and and_e (and_e_out, end_ad_out, b_e);
  _8Register u_8register_1 (
    .out_4(n8register_1_out_4), .in_2(controlled_buffer_1_out), .in_3(and_e_out), .in_1(and_s_out));
endmodule
